# Fritzing sketch triggerbox (saved by Fritzing 0.8.3b)
circuit board: 13.2644cm x 5.56918cm
stripboards: 1

parts:
  LED1 = LED - 5mm [color="Red (633nm)" package="5 mm [THT]"]
  R1 = Resistor [tolerance=±5% resistance=220 package=THT]
  IC2 = MCP4822 [package=DIL]
  Part1 = Arduino Nano (Rev3.0)
  U1 = BNC [package=bnc]
  U2 = BNC [package=bnc]
  U3 = BNC [package=bnc]
  U4 = BNC [package=bnc]
  U5 = BNC [package=bnc]

nets:
  N1: LED1.cathode, R1.Pin_1
  N2: LED1.anode, Part1.D2
  GND: R1.Pin_0, IC2.Vss, Part1.GND, U1.GND, U2.GND, U3.GND, U4.GND, U5.GND
  VDD: IC2.Vdd, Part1.5V
  N3: IC2.CS, Part1.D10
  N4: IC2.SCK, Part1.D13/SCK
  N5: IC2.SDI, Part1.D11/MOSI
  N6: IC2.LDAC, Part1.D7
  N7: IC2.Voutb, U2.OUT
  N8: IC2.Vouta, U1.OUT
  N9: Part1.D9, U3.OUT
  N10: Part1.A1, U5.OUT
  N11: Part1.A0, U4.OUT

notes:
  strawlab triggerbox v1.0
  Sep-2013
